// Logisim project fullAdder.circ as structural Verilog: 1 circuit, main circuit main
module main (
  input  A,
  input  B,
  input  Cin,
  input  a0,
  input  a1,
  input  a2,
  input  a3,
  input  b0,
  input  b1,
  input  b2,
  input  b3,
  input  in_12
);

  wire n7408_1_pin3, n7408_1_pin8, n7408_1_pin10, n7408_2_pin3, n7408_2_pin8, n7408_2_pin10, n7408_3_pin3,
       n7408_3_pin8, n7408_3_pin10, n7408_4_pin3, n7408_4_pin8, n7408_4_pin10, n7408_5_pin3, n7408_5_pin8,
       n7408_5_pin10, n7432_1_pin2, n7432_1_pin3, n7432_1_pin4, n7432_1_pin5, n7432_1_pin6, n7432_1_pin8,
       n7432_2_pin2, n7432_2_pin3, n7432_2_pin4, n7432_2_pin5, n7432_2_pin6, n7432_2_pin8, n7432_3_pin2,
       n7432_3_pin3, n7432_3_pin4, n7432_3_pin5, n7432_3_pin6, n7432_3_pin8, n7432_4_pin2, n7432_4_pin3,
       n7432_4_pin4, n7432_4_pin5, n7432_4_pin6, n7432_4_pin8, n7432_5_pin2, n7432_5_pin3, n7432_5_pin4,
       n7432_5_pin5, n7432_5_pin6, n7432_5_pin8, n7486_1_pin6, n7486_2_pin6, n7486_3_pin6, n7486_4_pin6,
       n7486_5_pin6;

  _7408 #(.ShowInternalStructure("true")) u_7408_1 (
    .pin1(B), .pin2(A), .pin3(n7408_1_pin3), .pin10(n7408_1_pin10), .pin9(Cin), .pin8(n7408_1_pin8));  // open: pin4, pin5, pin6, pin13, pin12, pin11
  _7432 #(.ShowInternalStructure("true")) u_7432_1 (
    .pin2(n7432_1_pin2), .pin3(n7432_1_pin3), .pin4(n7432_1_pin4), .pin5(n7432_1_pin5), .pin6(n7432_1_pin6),
    .pin10(n7408_1_pin3), .pin9(n7408_1_pin8), .pin8(n7432_1_pin8));  // open: pin1, pin13, pin12, pin11
  _7486 #(.ShowInternalStructure("true")) u_7486_1 (
    .pin1(B), .pin2(A), .pin3(n7408_1_pin10), .pin4(n7408_1_pin10), .pin5(Cin), .pin6(n7486_1_pin6),
    .pin13(n7432_1_pin2), .pin12(n7432_1_pin3), .pin11(n7432_1_pin4), .pin10(n7432_1_pin5),
    .pin9(n7432_1_pin6));  // open: pin8
  _7408 #(.ShowInternalStructure("true")) u_7408_2 (
    .pin1(b0), .pin2(a0), .pin3(n7408_2_pin3), .pin10(n7408_2_pin10), .pin9(in_12), .pin8(n7408_2_pin8));  // open: pin4, pin5, pin6, pin13, pin12, pin11
  _7432 #(.ShowInternalStructure("true")) u_7432_2 (
    .pin2(n7432_2_pin2), .pin3(n7432_2_pin3), .pin4(n7432_2_pin4), .pin5(n7432_2_pin5), .pin6(n7432_2_pin6),
    .pin10(n7408_2_pin3), .pin9(n7408_2_pin8), .pin8(n7432_2_pin8));  // open: pin1, pin13, pin12, pin11
  _7486 #(.ShowInternalStructure("true")) u_7486_2 (
    .pin1(b0), .pin2(a0), .pin3(n7408_2_pin10), .pin4(n7408_2_pin10), .pin5(in_12), .pin6(n7486_2_pin6),
    .pin13(n7432_2_pin2), .pin12(n7432_2_pin3), .pin11(n7432_2_pin4), .pin10(n7432_2_pin5),
    .pin9(n7432_2_pin6));  // open: pin8
  LED S (.in(n7486_1_pin6));
  LED S0 (.in(n7486_2_pin6));
  LED Cout (.in(n7432_1_pin8));
  LED Cout0 (.in(n7432_2_pin8));
  _7408 #(.ShowInternalStructure("true")) u_7408_3 (
    .pin1(b1), .pin2(a1), .pin3(n7408_3_pin3), .pin10(n7408_3_pin10), .pin9(n7432_2_pin8), .pin8(n7408_3_pin8));  // open: pin4, pin5, pin6, pin13, pin12, pin11
  _7432 #(.ShowInternalStructure("true")) u_7432_3 (
    .pin2(n7432_3_pin2), .pin3(n7432_3_pin3), .pin4(n7432_3_pin4), .pin5(n7432_3_pin5), .pin6(n7432_3_pin6),
    .pin10(n7408_3_pin3), .pin9(n7408_3_pin8), .pin8(n7432_3_pin8));  // open: pin1, pin13, pin12, pin11
  _7486 #(.ShowInternalStructure("true")) u_7486_3 (
    .pin1(b1), .pin2(a1), .pin3(n7408_3_pin10), .pin4(n7408_3_pin10), .pin5(n7432_2_pin8),
    .pin6(n7486_3_pin6), .pin13(n7432_3_pin2), .pin12(n7432_3_pin3), .pin11(n7432_3_pin4),
    .pin10(n7432_3_pin5), .pin9(n7432_3_pin6));  // open: pin8
  LED Cout1 (.in(n7432_3_pin8));
  LED S1 (.in(n7486_3_pin6));
  _7408 #(.ShowInternalStructure("true")) u_7408_4 (
    .pin1(b2), .pin2(a2), .pin3(n7408_4_pin3), .pin10(n7408_4_pin10), .pin9(n7432_3_pin8), .pin8(n7408_4_pin8));  // open: pin4, pin5, pin6, pin13, pin12, pin11
  _7432 #(.ShowInternalStructure("true")) u_7432_4 (
    .pin2(n7432_4_pin2), .pin3(n7432_4_pin3), .pin4(n7432_4_pin4), .pin5(n7432_4_pin5), .pin6(n7432_4_pin6),
    .pin10(n7408_4_pin3), .pin9(n7408_4_pin8), .pin8(n7432_4_pin8));  // open: pin1, pin13, pin12, pin11
  _7486 #(.ShowInternalStructure("true")) u_7486_4 (
    .pin1(b2), .pin2(a2), .pin3(n7408_4_pin10), .pin4(n7408_4_pin10), .pin5(n7432_3_pin8),
    .pin6(n7486_4_pin6), .pin13(n7432_4_pin2), .pin12(n7432_4_pin3), .pin11(n7432_4_pin4),
    .pin10(n7432_4_pin5), .pin9(n7432_4_pin6));  // open: pin8
  LED S2 (.in(n7486_4_pin6));
  LED Cout2 (.in(n7432_4_pin8));
  _7408 #(.ShowInternalStructure("true")) u_7408_5 (
    .pin1(a3), .pin2(b3), .pin3(n7408_5_pin3), .pin10(n7408_5_pin10), .pin9(n7432_4_pin8), .pin8(n7408_5_pin8));  // open: pin4, pin5, pin6, pin13, pin12, pin11
  _7432 #(.ShowInternalStructure("true")) u_7432_5 (
    .pin2(n7432_5_pin2), .pin3(n7432_5_pin3), .pin4(n7432_5_pin4), .pin5(n7432_5_pin5), .pin6(n7432_5_pin6),
    .pin10(n7408_5_pin3), .pin9(n7408_5_pin8), .pin8(n7432_5_pin8));  // open: pin1, pin13, pin12, pin11
  _7486 #(.ShowInternalStructure("true")) u_7486_5 (
    .pin1(a3), .pin2(b3), .pin3(n7408_5_pin10), .pin4(n7408_5_pin10), .pin5(n7432_4_pin8),
    .pin6(n7486_5_pin6), .pin13(n7432_5_pin2), .pin12(n7432_5_pin3), .pin11(n7432_5_pin4),
    .pin10(n7432_5_pin5), .pin9(n7432_5_pin6));  // open: pin8
  LED Cout3 (.in(n7432_5_pin8));
  LED S3 (.in(n7486_5_pin6));

  // Notes on the sheet:
  //   1 + 3 = 4 (0100)
endmodule
