// Logisim project halfAdd.circ as structural Verilog: 1 circuit, main circuit main
module main (
  input  a,
  input  b
);

  wire n7408_1_pin2, n7408_1_pin3, n7408_1_pin4, n7408_1_pin5, n7408_1_pin6, n7408_1_pin11, n7486_1_pin3;

  _7408 #(.ShowInternalStructure("true")) u_7408_1 (
    .pin2(n7408_1_pin2), .pin3(n7408_1_pin3), .pin4(n7408_1_pin4), .pin5(n7408_1_pin5), .pin6(n7408_1_pin6),
    .pin13(b), .pin12(a), .pin11(n7408_1_pin11));  // open: pin1, pin10, pin9, pin8
  _7486 #(.ShowInternalStructure("true")) u_7486_1 (
    .pin1(b), .pin2(a), .pin3(n7486_1_pin3), .pin13(n7408_1_pin2), .pin12(n7408_1_pin3),
    .pin11(n7408_1_pin4), .pin10(n7408_1_pin5), .pin9(n7408_1_pin6));  // open: pin4, pin5, pin6, pin8
  LED Sum (.in(n7408_1_pin11));
  LED Carry (.in(n7486_1_pin3));
endmodule
