// Logisim project mult4.circ as structural Verilog: 1 circuit, main circuit main
module main (
  input  A3,
  input  A2,
  input  A1,
  input  A0,
  input  B3,
  input  B2,
  input  B1,
  input  B0
);

  wire adder_1_cout, adder_1_out, adder_2_cout, adder_2_out, adder_3_cout, adder_3_out, adder_4_cout,
       adder_4_out, adder_5_cout, adder_5_out, adder_6_cout, adder_6_out, adder_7_cout, adder_7_out,
       adder_8_cout, adder_8_out, adder_9_cout, adder_9_out, adder_10_cout, adder_10_out, adder_11_cout,
       adder_11_out, adder_12_cout, adder_12_out, adder_13_cout, adder_13_out, adder_14_cout, adder_14_out,
       adder_15_cout, adder_15_out, adder_16_out, and_1_out, and_2_out, and_3_out, and_4_out, and_5_out,
       and_6_out, and_7_out, and_8_out, and_9_out, and_10_out, and_11_out, and_12_out, and_13_out,
       and_14_out, and_15_out, and_16_out;

  and and_1 (and_1_out, B0, A0);
  and and_2 (and_2_out, B0, A1);
  and and_3 (and_3_out, A0, B1);
  and and_4 (and_4_out, A2, B0);
  and and_5 (and_5_out, A1, B1);
  and and_6 (and_6_out, B2, A0);
  and and_7 (and_7_out, A3, B0);
  and and_8 (and_8_out, A2, B1);
  and and_9 (and_9_out, A1, B2);
  and and_10 (and_10_out, A0, B3);
  and and_11 (and_11_out, A3, B1);
  and and_12 (and_12_out, A2, B2);
  and and_13 (and_13_out, A1, B3);
  and and_14 (and_14_out, A3, B2);
  and and_15 (and_15_out, A2, B3);
  and and_16 (and_16_out, B3, A3);
  Adder #(.width(1)) adder_1 (.a(and_2_out), .b(and_3_out), .out(adder_1_out), .cin(1'b0), .cout(adder_1_cout));
  Adder #(.width(1)) adder_2 (.a(and_4_out), .b(and_5_out), .out(adder_2_out), .cin(adder_1_cout), .cout(adder_2_cout));
  Adder #(.width(1)) adder_3 (.a(and_7_out), .b(and_8_out), .out(adder_3_out), .cin(adder_2_cout), .cout(adder_3_cout));
  Adder #(.width(1)) adder_4 (
    .a(and_11_out), .b(and_12_out), .out(adder_4_out), .cin(adder_3_cout), .cout(adder_4_cout));
  Adder #(.width(1)) adder_5 (
    .a(and_14_out), .b(and_15_out), .out(adder_5_out), .cin(adder_4_cout), .cout(adder_5_cout));
  Adder #(.width(1)) adder_6 (.a(and_16_out), .b(1'b0), .out(adder_6_out), .cin(adder_5_cout), .cout(adder_6_cout));
  Adder #(.width(1)) adder_7 (.a(adder_2_out), .b(and_6_out), .out(adder_7_out), .cin(1'b0), .cout(adder_7_cout));
  Adder #(.width(1)) adder_8 (
    .a(adder_3_out), .b(and_9_out), .out(adder_8_out), .cin(adder_7_cout), .cout(adder_8_cout));
  Adder #(.width(1)) adder_9 (
    .a(adder_4_out), .b(and_13_out), .out(adder_9_out), .cin(adder_8_cout), .cout(adder_9_cout));
  Adder #(.width(1)) adder_10 (.a(adder_9_cout), .b(adder_5_out), .out(adder_10_out), .cin(1'b0), .cout(adder_10_cout));
  Adder #(.width(1)) adder_11 (
    .a(adder_10_cout), .b(adder_6_out), .out(adder_11_out), .cin(1'b0), .cout(adder_11_cout));
  LED led_1 (.in(and_1_out));
  LED led_2 (.in(adder_1_out));
  LED led_3 (.in(adder_7_out));
  Adder #(.width(1)) adder_12 (.a(adder_8_out), .b(and_10_out), .out(adder_12_out), .cin(1'b0), .cout(adder_12_cout));
  LED led_4 (.in(adder_12_out));
  Adder #(.width(1)) adder_13 (
    .a(adder_12_cout), .b(adder_9_out), .out(adder_13_out), .cin(1'b0), .cout(adder_13_cout));
  LED led_5 (.in(adder_13_out));
  Adder #(.width(1)) adder_14 (
    .a(adder_13_cout), .b(adder_10_out), .out(adder_14_out), .cin(1'b0), .cout(adder_14_cout));
  LED led_6 (.in(adder_14_out));
  Adder #(.width(1)) adder_15 (
    .a(adder_14_cout), .b(adder_11_out), .out(adder_15_out), .cin(1'b0), .cout(adder_15_cout));
  LED led_7 (.in(adder_15_out));
  Adder #(.width(1)) adder_16 (
    .a(adder_6_cout), .b(adder_11_cout), .out(adder_16_out), .cin(adder_15_cout));  // open: cout
  LED led_8 (.in(adder_16_out));
endmodule
